# Fritzing sketch wheater (saved by Fritzing 0.9.2b)
breadboards: 1

parts:
  Part1 = Arduino Uno (Rev3)
  T1 = LM35 Temperature Sensor [package="TO92 [THT]"]
  R1 = Resistor [tolerance=±5% resistance=4.7k package=THT]
  RHT1 = Humidity and Temperature Sensor RHT03
  R2 = Resistor [tolerance=±5% resistance=10k package=THT]
  U1 = HIH-4030 [package=hih-4030]
  R3 = Photocell (LDR) [package=THT]
  R4 = Resistor [tolerance=±5% resistance=10k package=THT]
  Part15 = FC-28 Soil Hygrometer Module - Probe
  Part16 = FC-28 Soil Hygrometer Module
  SD_card_module1 = SD Card Module
  R5 = Resistor [tolerance=±5% resistance=47 package=THT]
  R6 = Resistor [tolerance=±5% resistance=47 package=THT]
  R7 = Resistor [tolerance=±5% resistance=47 package=THT]
  R8 = Resistor [tolerance=±5% resistance=100 package=THT]
  R9 = Resistor [tolerance=±5% resistance=100 package=THT]
  R10 = Resistor [tolerance=±5% resistance=100 package=THT]
  Part18 = Adafruit BMP180

nets:
  N1: Part1.A0, U1.OUT
  N2: Part1.A1, R3.pin_1, R4.Pin_0
  N3: Part1.A2, Part16.AO
  N4: Part1.A4/SDA, Part18.SDA
  N5: Part1.A5/SCL, Part18.SCL
  N6: Part1.D11_PWM/MOSI, R6.Pin_1, R9.Pin_0
  N7: Part1.D12/MISO, SD_card_module1.MISO
  N8: Part1.D13/SCK, R7.Pin_1, R10.Pin_0
  N9: Part1.D2, T1.Vout, R1.Pin_0
  N10: Part1.D3_PWM, RHT1.Data-signal, R2.Pin_1
  N11: Part1.D5_PWM, R5.Pin_1, R8.Pin_0
  3V3: Part1.3V3, Part16.VCC
  VCC: Part1.5V, T1.+Vs, R1.Pin_1, RHT1.Vcc, R2.Pin_0, U1.VCC, R4.Pin_1
  GND: Part1.GND, T1.GND, RHT1.GND_2, U1.GND, R3.pin_0, Part16.GND, R8.Pin_1, R9.Pin_1, R10.Pin_1, Part18.GND
  N12: Part15.POS, Part16.POS
  N13: Part15.NEG, Part16.NEG
  N14: SD_card_module1.CS, R5.Pin_0
  N15: SD_card_module1.MOSI, R6.Pin_0
  N16: SD_card_module1.SCK, R7.Pin_0

notes:
  VIN 3.3V

custom parts:
  FC-28 Soil Hygrometer Module - Probe: The FC-28 is a soil hygrometer module that uses the Texas Instruments LM393 comparator chip to provide an analog measurement of soil humidity.
  FC-28 Soil Hygrometer Module: The FC-28 is a soil hygrometer module that uses the Texas Instruments LM393 comparator chip to provide an analog measurement of soil humidity. The digital output is high when soil moisture is over a certain threshold, as determined by adjusting the potentiometer.
  SD Card Module: SD Card Module Slot Socket Reader For Arduino ARM MCU
  Adafruit BMP180: This precision sensor from Bosch is the best low-cost sensing solution for measuring barometric pressure and temperature. Because pressure changes with altitude you can also use it as an altimeter! The sensor is soldered onto a PCB with a 3.3V regulator, I2C level shifter and pull-up resistors on the I2C pins. The BMP180 is the next-generation of sensors from Bosch, and replaces the BMP085.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
